# Fritzing sketch nanorover (saved by Fritzing 0.8.0b)
breadboards: 1

parts:
  Part1 = Arduino Nano (Rev3.0)
  J1 = Basic Servo
  J2 = Basic Servo
  Part2 = SRF05 Ultrasonic Rangefinder

nets:
  GND: Part1.GND, J1.gnd, J2.gnd, Part2.GND
  N1: Part1.D2, J1.pulse
  N2: Part1.D4, J2.pulse
  N3: Part1.D12/MISO, Part2.Echo
  VCC: Part1.VIN, Part1.5V, J1.vcc, J2.vcc, Part2.VCC
  N4: Part1.D13/SCK, Part2.Trig
